// Logisim project LAB_01_Simulation - Digital Logic Gates and Boolean Function.circ as structural Verilog: 1 circuit, main circuit main
module main (
  input  A,
  input  C,
  input  A_2,
  input  B,
  input  B_2,
  input  C_2,
  output F
);

  wire and_1_out, and_2_out, and_3_out, not_1_out, not_2_out, or_1_out;

  not not_1 (not_1_out, A);
  not not_2 (not_2_out, B);
  and and_1 (and_1_out, not_1_out, C);
  and and_2 (and_2_out, A_2, not_2_out);
  and and_3 (and_3_out, B_2, C_2);
  or or_1 (or_1_out, and_1_out, and_2_out);
  or or_2 (F, or_1_out, and_3_out);

  // Notes on the sheet:
  //   I1
  //   I2
  //   I3
  //   Section: 09
  //   CSE231L
  //   Spring 2024
  //   Name:  Sudipto Roy
  //   ID: 2222756042
endmodule
