// Logisim project LAB2-1st_Canonical_Form.circ as structural Verilog: 1 circuit, main circuit main
module main (
  input  in_1,
  input  in_2,
  input  in_3,
  output out_4
);

  wire and_1_out, and_2_out, and_3_out, not_1_out, not_2_out, not_3_out, or_1_out;

  not not_1 (not_1_out, in_1);
  not not_2 (not_2_out, in_2);
  not not_3 (not_3_out, in_3);
  and and_1 (and_1_out, not_1_out, not_2_out, in_3);
  and and_2 (and_2_out, not_1_out, in_2, not_3_out);
  and and_3 (and_3_out, in_1, in_2, not_3_out);
  or or_1 (or_1_out, and_1_out, and_2_out);
  or or_2 (out_4, or_1_out, and_3_out);

  // Notes on the sheet:
  //   A'
  //   A
  //   B'
  //   B
  //   C'
  //   C
  //   A'B'C
  //   A'BC'
  //   ABC'
  //   Simulation -1 : 1st Canonical Form
  //   A'B'C+A'BC'
  //   A'B'C+A'BC'+ABC'
  //   ID: 2222756042
  //   CSE231
  //   Section: 09
  //   Name: Sudipto Roy
endmodule
