// Logisim project LAB2-2nd_Canonical_Form.circ as structural Verilog: 1 circuit, main circuit main
module main (
  input  in_1,
  input  in_2,
  input  in_3,
  output out_4
);

  wire and_1_out, not_1_out, not_2_out, not_3_out, or_1_out, or_2_out, or_3_out, or_4_out, or_5_out;

  not not_1 (not_1_out, in_1);
  not not_2 (not_2_out, in_2);
  not not_3 (not_3_out, in_3);
  or or_1 (or_1_out, in_1, in_2, in_3);
  or or_2 (or_2_out, in_1, not_2_out, not_3_out);
  or or_3 (or_3_out, not_1_out, in_2, in_3);
  or or_4 (or_4_out, not_1_out, in_2, not_3_out);
  or or_5 (or_5_out, not_1_out, not_2_out, not_3_out);
  and and_1 (and_1_out, or_1_out, or_2_out, or_3_out);
  and and_2 (out_4, and_1_out, or_4_out, or_5_out);

  // Notes on the sheet:
  //   A'
  //   A
  //   B'
  //   B
  //   C
  //   C'
  //   A+B+C
  //   A+B'+C'
  //   A'+B+C
  //   A'+B+C'
  //   A'+B'+C'
  //   (A+B+C)(A+B'+C')+(A'+B+C)
  //   Simulation -2 : 2nd Canonical Form
  //   ID: 2222756042
  //   CSE231
  //   Section: 09
  //   Name: Sudipto Roy
  //   (A+B+C)(A+B'+C')+(A'+B+C)(A'+B+C')(A'+B'+C')
endmodule
