// Logisim project LAB_04_Simulation - Combinational_Logic_Design_II.circ as structural Verilog: 1 circuit, main circuit main
module main (
  input  in_1,
  input  in_2,
  input  in_3,
  input  in_4,
  output [3:0] Output
);

  wire nor_1_out, nor_2_out, nor_4_out, nor_5_out, nor_6_out, nor_7_out, nor_8_out, nor_9_out, nor_10_out,
       nor_11_out, nor_12_out, nor_13_out, nor_14_out, nor_15_out, nor_16_out, nor_17_out, nor_18_out,
       nor_19_out, nor_20_out, nor_21_out, nor_22_out, nor_23_out, nor_24_out, nor_26_out, nor_27_out;

  nor nor_1 (nor_1_out, in_2, in_2);
  nor nor_2 (nor_2_out, in_3, in_3);
  nor nor_3 (Output[0], in_4, in_4);
  nor nor_4 (nor_4_out, in_3, in_4);
  nor nor_5 (nor_5_out, in_1, in_1);
  nor nor_6 (nor_6_out, nor_5_out, nor_7_out);
  nor nor_7 (nor_7_out, in_2, in_2);
  nor nor_8 (nor_8_out, in_1, in_1);
  nor nor_9 (nor_9_out, nor_8_out, nor_10_out, nor_11_out);
  nor nor_10 (nor_10_out, in_3, in_3);
  nor nor_11 (nor_11_out, in_4, in_4);
  nor nor_12 (nor_12_out, nor_1_out, nor_1_out);
  nor nor_13 (nor_13_out, nor_12_out, nor_14_out);
  nor nor_14 (nor_14_out, nor_2_out, nor_2_out);
  nor nor_15 (nor_15_out, nor_1_out, nor_1_out);
  nor nor_16 (nor_16_out, nor_15_out, nor_17_out);
  nor nor_17 (nor_17_out, Output[0], Output[0]);
  nor nor_18 (nor_18_out, in_2, in_2);
  nor nor_19 (nor_19_out, nor_18_out, nor_20_out, nor_21_out);
  nor nor_20 (nor_20_out, in_3, in_3);
  nor nor_21 (nor_21_out, in_4, in_4);
  nor nor_22 (nor_22_out, in_3, nor_4_out);
  nor nor_23 (nor_23_out, nor_22_out, nor_24_out);
  nor nor_24 (nor_24_out, nor_4_out, in_4);
  nor nor_25 (Output[1], nor_23_out, nor_23_out);
  nor nor_26 (nor_26_out, nor_6_out, nor_9_out);
  nor nor_27 (nor_27_out, nor_13_out, nor_16_out, nor_19_out);
  nor nor_28 (Output[3], nor_26_out, nor_26_out);
  nor nor_29 (Output[2], nor_27_out, nor_27_out);

  // Notes on the sheet:
  //   Name: Sudipto Roy
  //   ID: 2222756042
  //   Section: 09
  //   CSE231L
  //   Spring 2024
endmodule
