// Logisim project LAB_09_Simulation - Synchronous Sequential Circuits.circ as structural Verilog: 1 circuit, main circuit main
module main (
  input  X,
  input  X_2,
  input  X_3
);

  wire and_1_out, and_2_out, and_3_out, and_4_out, and_5_out, and_6_out, and_7_out, and_8_out, and_9_out,
       clock_1_out, clock_2_out, clock_3_out, d_ff_1_q, d_ff_1_qn, d_ff_2_q, j_k_ff_1_q, j_k_ff_1_qn,
       j_k_ff_2_q, not_1_out, not_2_out, not_3_out, or_1_out, or_2_out, t_ff_1_q, t_ff_1_qn, t_ff_2_q,
       t_ff_2_qn;

  not not_1 (not_1_out, X);
  not not_2 (not_2_out, X_3);
  and and_1 (and_1_out, j_k_ff_1_qn, not_1_out);
  Clock clock_1 (.out(clock_1_out));
  and and_2 (and_2_out, t_ff_1_qn, t_ff_2_qn, not_2_out);
  or or_1 (or_1_out, and_2_out, and_3_out);
  and and_3 (and_3_out, t_ff_2_q, X_3);
  J_K_Flip_Flop j_k_ff_1 (
    .J(X), .clk(clock_1_out), .K(X), .Q(j_k_ff_1_q), .Qn(j_k_ff_1_qn));  // open: preset, en, reset
  J_K_Flip_Flop j_k_ff_2 (.J(and_1_out), .clk(clock_1_out), .K(X), .Q(j_k_ff_2_q));  // open: Qn, preset, en, reset
  Clock clock_2 (.out(clock_2_out));
  and and_4 (and_4_out, j_k_ff_1_qn, X);
  T_Flip_Flop t_ff_1 (.clk(clock_2_out), .T(X_3), .Q(t_ff_1_q), .Qn(t_ff_1_qn));  // open: preset, reset, en
  T_Flip_Flop t_ff_2 (.clk(clock_2_out), .T(or_1_out), .Q(t_ff_2_q), .Qn(t_ff_2_qn));  // open: preset, reset, en
  LED led_1 (.in(j_k_ff_1_q));
  LED led_2 (.in(j_k_ff_2_q));
  LED led_3 (.in(and_4_out));
  LED led_4 (.in(t_ff_1_q));
  LED led_5 (.in(t_ff_2_q));
  LED led_6 (.in(and_5_out));
  and and_5 (and_5_out, t_ff_1_qn, X_3);
  not not_3 (not_3_out, X_2);
  and and_6 (and_6_out, d_ff_1_qn, X_2);
  or or_2 (or_2_out, and_6_out, and_7_out);
  and and_7 (and_7_out, d_ff_1_q, not_3_out);
  and and_8 (and_8_out, d_ff_1_qn, not_3_out);
  Clock clock_3 (.out(clock_3_out));
  D_Flip_Flop d_ff_1 (.clk(clock_3_out), .D(or_2_out), .Q(d_ff_1_q), .Qn(d_ff_1_qn));  // open: preset, en, reset
  D_Flip_Flop d_ff_2 (.clk(clock_3_out), .D(and_8_out), .Q(d_ff_2_q));  // open: Qn, preset, en, reset
  and and_9 (and_9_out, d_ff_1_qn, X_2);
  LED led_7 (.in(d_ff_1_q));
  LED led_8 (.in(d_ff_2_q));
  LED led_9 (.in(and_9_out));

  // Notes on the sheet:
  //   Circuit Simulation using JK Flip-Flops
  //   Circuit Simulation using T Flip-Flops
  //   A
  //   B
  //   Y
  //   A
  //   B
  //   Y
  //   Circuit Simulation using D Flip-Flops
  //   Name: Sudipto Roy
  //   ID: 2222756042
  //   Section: 09
  //   CSE231L
  //   Spring'2024
  //   A
  //   B
  //   Y
endmodule
